# Fritzing sketch wiring (saved by Fritzing 0.9.2b)

parts:
  Nokia_5110_LCD_Module1 = Nokia 5110 LCD
  WeMos_D1_Mini1 = WeMos D1 Mini
  WeMos_D1_Mini2 = WeMos D1 Mini
  Nokia_5110_LCD_Module3 = Nokia 5110 LCD

nets:
  VCC: Nokia_5110_LCD_Module1.VCC, WeMos_D1_Mini1.3V3
  N1: Nokia_5110_LCD_Module1.GND, Nokia_5110_LCD_Module1.RST, WeMos_D1_Mini1.G
  N2: Nokia_5110_LCD_Module1.SCE, WeMos_D1_Mini1.D1
  N3: Nokia_5110_LCD_Module1.D/C, WeMos_D1_Mini1.D4
  N4: Nokia_5110_LCD_Module1.DN(MOSI), WeMos_D1_Mini1.D7
  N5: Nokia_5110_LCD_Module1.SCLK, WeMos_D1_Mini1.D5
  N6: Nokia_5110_LCD_Module1.LED, WeMos_D1_Mini1.D0
  3V3: WeMos_D1_Mini2.3V3, Nokia_5110_LCD_Module3.VCC
  N7: WeMos_D1_Mini2.D0, Nokia_5110_LCD_Module3.Clk
  N8: WeMos_D1_Mini2.D4, Nokia_5110_LCD_Module3.BL
  N9: WeMos_D1_Mini2.D5, Nokia_5110_LCD_Module3.Din
  N10: WeMos_D1_Mini2.D6, Nokia_5110_LCD_Module3.DC
  N11: WeMos_D1_Mini2.D7, Nokia_5110_LCD_Module3.CE
  N12: WeMos_D1_Mini2.D8, Nokia_5110_LCD_Module3.RST
  N13: WeMos_D1_Mini2.G, Nokia_5110_LCD_Module3.Gnd

custom parts:
  Nokia 5110 LCD: Nokia 5110 Graphic 84*48 LCD module such as the Sparkfun LCD-10168 or the clones from Ebay. There is example code for the Arduino available from the Sparkfun site in https://learn.sparkfun.com/tutorials/graphic-lcd-hookup-guide This is a 3.3V device, if you are running it from a 5V micro you need a 5V tolorant level translator such as the 74ahc367 to protect the signal imputs. Rafa G. did a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
  Nokia 5110 LCD: Nokia 5110 Graphic 84*48 LCD module such as the Sparkfun LCD-10168 or the clones from Ebay. There is example code for the Arduino available from the Sparkfun site in https://learn.sparkfun.com/tutorials/graphic-lcd-hookup-guide This is a 3.3V device, if you are running it from a 5V micro you need a 5V tolorant level translator such as the 74ahc367 to protect the signal imputs. Rafa G. did a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
